# Fritzing sketch Untitled Sketch (saved by Fritzing 0.9.3b)

parts:
  S1 = H-Bridge with L298N
  Часть1 = Arduino Uno (Rev3)

nets:
  12V: S1.12V, Часть1.VIN
  GND: S1.GND, Часть1.GND
  N1: S1.IN1, Часть1.D11_PWM/MOSI
  N2: S1.IN2, Часть1.D10_PWM/SS
  N3: S1.IN3, Часть1.D9_PWM

notes:
  12 Вольт
  Лента

custom parts:
  H-Bridge with L298N: h-bridge
